# Fritzing sketch esquematico (saved by Fritzing 0.9.3b)
breadboards: 1

parts:
  GALILEO = Intel Galileo

nets:
  SENSOR 0: GALILEO.A0
  SENSOR 1: GALILEO.A1
  SENSOR 2: GALILEO.A2
  SENSOR 3: GALILEO.A3
  SENSOR 4: GALILEO.A4/SDA
  SAIDA Y: GALILEO.D9_PWM
