# Fritzing sketch esquematico (saved by Fritzing 0.9.3b)
breadboards: 1

parts:
  Part1 = Intel Galileo
  ARDUINO_02 = Arduino Uno (Rev3) - ICSP
  ARDUINO_01 = Arduino Uno (Rev3) - ICSP

nets:
  N1: Part1.ICSP_MISO, Part1.D12/MISO, ARDUINO_02.ICSP_MISO, ARDUINO_02.D12/MISO
  N2: Part1.ICSP_SCK, Part1.D13/SCK, ARDUINO_02.ICSP_SCK, ARDUINO_02.D13/SCK, ARDUINO_01.ICSP_SCK, ARDUINO_01.D13/SCK
  N3: Part1.ICSP_MOSI, Part1.D11_PWM/MOSI, ARDUINO_02.ICSP_MOSI, ARDUINO_02.D11_PWM/MOSI, ARDUINO_01.ICSP_MOSI, ARDUINO_01.D11_PWM/MOSI
  N4: Part1.D8, ARDUINO_02.D10_PWM/SS
  N5: Part1.D9_PWM, ARDUINO_01.D10_PWM/SS
