# Fritzing sketch esquematico (saved by Fritzing 0.9.3b)
breadboards: 1

parts:
  ARDUINO = Arduino Uno (Rev3) - ICSP
  GALILEO = Intel Galileo

nets:
  N1: ARDUINO.D0/RX, GALILEO.D1/TX
  N2: ARDUINO.D1/TX, GALILEO.D0/RX
